// Logisim project Processador.circ as structural Verilog: 6 circuits, main circuit main
module main (
  input  Reset,
  input  in_2,
  output [15:0] Read_Data
);

  wire and_1_out, clock_1__1, clock_1__2, clock_1__3, clock_1__4, clock_1__5, not_1_out, not_2_out, or_1_out,
       ula_1_zero, unidade_de_controle_1_aluadr, unidade_de_controle_1_aluscr, unidade_de_controle_1_branch,
       unidade_de_controle_1_jump, unidade_de_controle_1_memwrite, unidade_de_controle_1_rw,
       unidade_de_controle_1_ula_mem;
  wire [2:0] unidade_de_controle_1_ulaop;
  wire [3:0] conversor_de_saida_1_p2, conversor_de_saida_1_p3, conversor_de_saida_1_p4,
       conversor_de_saida_1_p5, conversor_de_saida_2_p2, conversor_de_saida_2_p3, conversor_de_saida_2_p4,
       conversor_de_saida_2_p5;
  wire [15:0] adder_1_out, banco_de_registradores_1_rx_2, banco_de_registradores_1_ry_2, bit_extender_1_out,
       bit_extender_2_out, bit_extender_3_out, multiplexer_1_out, multiplexer_2_out, multiplexer_3_out,
       multiplexer_4_out, ram_1_data, ram_2_data, register_1_q, ula_1_ula_result, undriven;

  Register #(.width(16)) register_1 (
    .D(multiplexer_4_out), .Q(register_1_q), .clk(clock_1__1), .clr(Reset));  // open: en
  assign bit_extender_1_out = {{15{1'b0}}, 1'b1};  // Bit_Extender bit_extender_1
  Adder #(.width(16)) adder_1 (.a(bit_extender_1_out), .b(register_1_q), .out(adder_1_out));  // open: cin, cout
  RAM #(.addrWidth(16), .dataWidth(16)) ram_1 (.addr(register_1_q), .data(ram_1_data));  // open: sel, clk, ld, clr
  Clock clock_1 (.Reset(Reset), ._1(clock_1__1), ._2(clock_1__2), ._3(clock_1__3), ._4(clock_1__4), ._5(clock_1__5));
  // Conversor_de_Saida conversor_de_saida_1: pin names not known; wires that end beside it: ram_1_data, conversor_de_saida_1_p2, conversor_de_saida_1_p3, conversor_de_saida_1_p4, conversor_de_saida_1_p5
  UNIDADE_DE_CONTROLE unidade_de_controle_1 (
    .ALUscr(unidade_de_controle_1_aluscr), .RW(unidade_de_controle_1_rw),
    .ALUadr(unidade_de_controle_1_aluadr), .ULA_MEM(unidade_de_controle_1_ula_mem),
    .MemWrite(unidade_de_controle_1_memwrite), .Branch(unidade_de_controle_1_branch),
    .ULAOP(unidade_de_controle_1_ulaop), .in_1(conversor_de_saida_1_p2[0]),
    .in_2(conversor_de_saida_1_p2[1]), .in_3(conversor_de_saida_1_p2[2]), .in_4(conversor_de_saida_1_p2[3]),
    .Jump(unidade_de_controle_1_jump));
  assign bit_extender_2_out = {{12{1'b0}}, conversor_de_saida_1_p5};  // Bit_Extender bit_extender_2
  not not_1 (not_1_out, 1'b1);
  Banco_de_Registradores banco_de_registradores_1 (
    .RegWrite(unidade_de_controle_1_rw), .Reset(Reset), .ClockWB(clock_1__5),
    .Dado_para_reg_destino(multiplexer_2_out), .RX_2(banco_de_registradores_1_rx_2),
    .RY_2(banco_de_registradores_1_ry_2), .RY(conversor_de_saida_1_p5), .RX(conversor_de_saida_1_p4),
    .RD(conversor_de_saida_1_p3), .ClockBR(clock_1__2));
  Multiplexer #(.width(16)) multiplexer_1 (
    .in0(banco_de_registradores_1_ry_2), .in1(bit_extender_2_out), .out(multiplexer_1_out),
    .sel(unidade_de_controle_1_aluscr));  // open: en
  assign bit_extender_3_out = {{15{1'b0}}, not_1_out};  // Bit_Extender bit_extender_3
  Multiplexer #(.width(16)) multiplexer_2 (
    .in0(ula_1_ula_result), .in1(Read_Data), .out(multiplexer_2_out), .sel(unidade_de_controle_1_ula_mem));  // open: en
  Hex_Digit_Display hex_digit_display_1 (.value(conversor_de_saida_2_p2));  // open: dp
  // Conversor_de_Saida conversor_de_saida_2: pin names not known; wires that end beside it: multiplexer_2_out, conversor_de_saida_2_p2, conversor_de_saida_2_p3, conversor_de_saida_2_p4, conversor_de_saida_2_p5
  ULA ula_1 (
    .Dado1(banco_de_registradores_1_rx_2), .Dado_2(multiplexer_3_out), .ULA_RESULT(ula_1_ula_result),
    .ULAOP(unidade_de_controle_1_ulaop), .Clock(clock_1__3), .in_1(Reset), .ZERO(ula_1_zero));
  Multiplexer #(.width(16)) multiplexer_3 (
    .in0(multiplexer_1_out), .in1(bit_extender_3_out), .out(multiplexer_3_out),
    .sel(unidade_de_controle_1_aluadr));  // open: en
  Hex_Digit_Display hex_digit_display_2 (.value(conversor_de_saida_2_p3));  // open: dp
  Hex_Digit_Display hex_digit_display_3 (.value(conversor_de_saida_2_p4));  // open: dp
  or or_1 (or_1_out, unidade_de_controle_1_jump, and_1_out);
  and and_1 (and_1_out, unidade_de_controle_1_branch, ula_1_zero);
  Hex_Digit_Display hex_digit_display_4 (.value(conversor_de_saida_2_p5));  // open: dp
  Multiplexer #(.width(16)) multiplexer_4 (
    .in0(adder_1_out), .in1(undriven), .out(multiplexer_4_out), .sel(or_1_out));  // open: en
  RAM #(.addrWidth(16), .dataWidth(16)) ram_2 (
    .addr(ula_1_ula_result), .data(ram_2_data), .clk(clock_1__4), .ld(not_2_out), .clr(in_2));  // open: sel
  not not_2 (not_2_out, unidade_de_controle_1_memwrite);
  assign ram_2_data = unidade_de_controle_1_memwrite ? banco_de_registradores_1_ry_2 : 16'bz;  // Controlled_Buffer controlled_buffer_1
  assign Read_Data = not_2_out ? ram_2_data : 16'bz;  // Controlled_Buffer controlled_buffer_2
endmodule

module Banco_de_Registradores (
  input  RegWrite,
  input  Reset,
  input  ClockWB,
  input  ClockBR,
  input  [15:0] Dado_para_reg_destino,
  input  [3:0] RD,
  input  [3:0] RX,
  input  [3:0] RY,
  output [15:0] RX_2,
  output [15:0] RY_2
);

  wire undriven;
  wire [3:0] demultiplexer_2_out3, demultiplexer_2_out7, demultiplexer_2_out11, demultiplexer_2_out15;
  wire [15:0] controlled_buffer_1_out, controlled_buffer_2_out, controlled_buffer_3_out,
       controlled_buffer_4_out, controlled_buffer_5_out, controlled_buffer_6_out, controlled_buffer_7_out,
       controlled_buffer_8_out, controlled_buffer_9_out, controlled_buffer_10_out, controlled_buffer_11_out,
       controlled_buffer_12_out, controlled_buffer_13_out, controlled_buffer_14_out,
       controlled_buffer_15_out, controlled_buffer_16_out, demultiplexer_1_out0, demultiplexer_1_out1,
       demultiplexer_1_out2, demultiplexer_1_out3, demultiplexer_1_out4, demultiplexer_1_out5,
       demultiplexer_1_out6, demultiplexer_1_out7, demultiplexer_1_out8, demultiplexer_1_out9,
       demultiplexer_1_out10, demultiplexer_1_out11, demultiplexer_1_out12, demultiplexer_1_out13,
       demultiplexer_1_out14, demultiplexer_1_out15, multiplexer_1_out, multiplexer_2_out, register_1_q,
       register_2_q, register_3_q, register_4_q, register_5_q, register_6_q, register_7_q, register_8_q,
       register_9_q, register_10_q, register_11_q, register_12_q, register_13_q, register_14_q,
       register_15_q, register_16_q;

  Demultiplexer #(.select(4), .width(16)) demultiplexer_1 (
    .out0(demultiplexer_1_out0), .out1(demultiplexer_1_out1), .out2(demultiplexer_1_out2),
    .out3(demultiplexer_1_out3), .out4(demultiplexer_1_out4), .out5(demultiplexer_1_out5),
    .out6(demultiplexer_1_out6), .out7(demultiplexer_1_out7), .out8(demultiplexer_1_out8),
    .out9(demultiplexer_1_out9), .out10(demultiplexer_1_out10), .out11(demultiplexer_1_out11),
    .out12(demultiplexer_1_out12), .out13(demultiplexer_1_out13), .out14(demultiplexer_1_out14),
    .out15(demultiplexer_1_out15), .in(Dado_para_reg_destino), .sel(RD));  // open: en
  assign controlled_buffer_1_out = demultiplexer_2_out3[3] ? demultiplexer_1_out0 : 16'bz;  // Controlled_Buffer controlled_buffer_1
  assign controlled_buffer_2_out = demultiplexer_2_out7[3] ? demultiplexer_1_out4 : 16'bz;  // Controlled_Buffer controlled_buffer_2
  assign controlled_buffer_3_out = demultiplexer_2_out11[3] ? demultiplexer_1_out8 : 16'bz;  // Controlled_Buffer controlled_buffer_3
  assign controlled_buffer_4_out = demultiplexer_2_out15[3] ? demultiplexer_1_out12 : 16'bz;  // Controlled_Buffer controlled_buffer_4
  assign controlled_buffer_5_out = demultiplexer_2_out3[2] ? demultiplexer_1_out1 : 16'bz;  // Controlled_Buffer controlled_buffer_5
  Register #(.width(16)) register_1 (
    .D(controlled_buffer_1_out), .en(1'b1), .Q(register_1_q), .clk(ClockWB), .clr(Reset));
  assign controlled_buffer_6_out = demultiplexer_2_out7[2] ? demultiplexer_1_out5 : 16'bz;  // Controlled_Buffer controlled_buffer_6
  Register #(.width(16)) register_2 (
    .D(controlled_buffer_2_out), .en(1'b1), .Q(register_2_q), .clk(ClockWB), .clr(Reset));
  assign controlled_buffer_7_out = demultiplexer_2_out11[2] ? demultiplexer_1_out9 : 16'bz;  // Controlled_Buffer controlled_buffer_7
  Register #(.width(16)) register_3 (
    .D(controlled_buffer_3_out), .en(1'b1), .Q(register_3_q), .clk(ClockWB), .clr(Reset));
  Register #(.width(16)) register_4 (
    .D(controlled_buffer_4_out), .en(1'b1), .Q(register_4_q), .clk(ClockWB), .clr(Reset));
  Register #(.width(16)) register_5 (
    .D(controlled_buffer_5_out), .en(1'b1), .Q(register_5_q), .clk(ClockWB), .clr(Reset));
  Register #(.width(16)) register_6 (
    .D(controlled_buffer_6_out), .en(1'b1), .Q(register_6_q), .clk(ClockWB), .clr(Reset));
  Register #(.width(16)) register_7 (
    .D(controlled_buffer_7_out), .en(1'b1), .Q(register_7_q), .clk(ClockWB), .clr(Reset));
  assign controlled_buffer_8_out = demultiplexer_2_out15[2] ? demultiplexer_1_out13 : 16'bz;  // Controlled_Buffer controlled_buffer_8
  Register #(.width(16)) register_8 (
    .D(controlled_buffer_8_out), .en(1'b1), .Q(register_8_q), .clk(ClockWB), .clr(Reset));
  Demultiplexer #(.select(4)) demultiplexer_2 (
    .out0(demultiplexer_2_out3[3]), .out1(demultiplexer_2_out3[2]), .out2(demultiplexer_2_out3[1]),
    .out3(demultiplexer_2_out3[0]), .out4(demultiplexer_2_out7[3]), .out5(demultiplexer_2_out7[2]),
    .out6(demultiplexer_2_out7[1]), .out7(demultiplexer_2_out7[0]), .out8(demultiplexer_2_out11[3]),
    .out9(demultiplexer_2_out11[2]), .out10(demultiplexer_2_out11[1]), .out11(demultiplexer_2_out11[0]),
    .out12(demultiplexer_2_out15[3]), .out13(demultiplexer_2_out15[2]), .out14(demultiplexer_2_out15[1]),
    .out15(demultiplexer_2_out15[0]), .in(RegWrite), .sel(RD));  // open: en
  assign controlled_buffer_9_out = demultiplexer_2_out3[1] ? demultiplexer_1_out2 : 16'bz;  // Controlled_Buffer controlled_buffer_9
  Register #(.width(16)) register_9 (
    .D(controlled_buffer_9_out), .en(1'b1), .Q(register_9_q), .clk(ClockWB), .clr(Reset));
  assign controlled_buffer_10_out = demultiplexer_2_out7[1] ? demultiplexer_1_out6 : 16'bz;  // Controlled_Buffer controlled_buffer_10
  Register #(.width(16)) register_10 (
    .D(controlled_buffer_10_out), .en(1'b1), .Q(register_10_q), .clk(ClockWB), .clr(Reset));
  assign controlled_buffer_11_out = demultiplexer_2_out11[1] ? demultiplexer_1_out10 : 16'bz;  // Controlled_Buffer controlled_buffer_11
  Register #(.width(16)) register_11 (
    .D(controlled_buffer_11_out), .en(1'b1), .Q(register_11_q), .clk(ClockWB), .clr(Reset));
  assign controlled_buffer_12_out = demultiplexer_2_out15[1] ? demultiplexer_1_out14 : 16'bz;  // Controlled_Buffer controlled_buffer_12
  Register #(.width(16)) register_12 (
    .D(controlled_buffer_12_out), .en(1'b1), .Q(register_12_q), .clk(ClockWB), .clr(Reset));
  assign controlled_buffer_13_out = demultiplexer_2_out3[0] ? demultiplexer_1_out3 : 16'bz;  // Controlled_Buffer controlled_buffer_13
  assign controlled_buffer_14_out = demultiplexer_2_out7[0] ? demultiplexer_1_out7 : 16'bz;  // Controlled_Buffer controlled_buffer_14
  assign controlled_buffer_15_out = demultiplexer_2_out11[0] ? demultiplexer_1_out11 : 16'bz;  // Controlled_Buffer controlled_buffer_15
  assign controlled_buffer_16_out = demultiplexer_2_out15[0] ? demultiplexer_1_out15 : 16'bz;  // Controlled_Buffer controlled_buffer_16
  Register #(.width(16)) register_13 (
    .D(controlled_buffer_13_out), .en(1'b1), .Q(register_13_q), .clk(ClockWB), .clr(Reset));
  Register #(.width(16)) register_14 (
    .D(controlled_buffer_14_out), .en(1'b1), .Q(register_14_q), .clk(ClockWB), .clr(Reset));
  Register #(.width(16)) register_15 (
    .D(controlled_buffer_15_out), .en(1'b1), .Q(register_15_q), .clk(ClockWB), .clr(Reset));
  Register #(.width(16)) register_16 (
    .D(controlled_buffer_16_out), .en(1'b1), .Q(register_16_q), .clk(ClockWB), .clr(Reset));
  Multiplexer #(.select(4), .width(16)) multiplexer_1 (
    .in0(register_1_q), .in1(register_5_q), .in2(register_9_q), .in3(register_13_q), .in4(register_2_q),
    .in5(register_6_q), .in6(register_10_q), .in7(register_14_q), .in8(register_3_q), .in9(register_11_q),
    .in10(register_7_q), .in11(register_15_q), .in12(register_4_q), .in13(register_8_q),
    .in14(register_12_q), .in15(register_16_q), .out(multiplexer_1_out), .sel(RX));  // open: en
  Register #(.width(16)) register_17 (.D(multiplexer_1_out), .Q(RX_2), .clk(ClockBR));  // open: en, clr
  Multiplexer #(.select(4), .width(16)) multiplexer_2 (
    .in0(register_1_q), .in1(register_5_q), .in2(register_9_q), .in3(register_13_q), .in4(register_2_q),
    .in5(register_6_q), .in6(register_10_q), .in7(register_14_q), .in8(register_3_q), .in9(register_11_q),
    .in10(register_7_q), .in11(register_15_q), .in12(register_4_q), .in13(register_8_q),
    .in14(register_12_q), .in15(register_16_q), .out(multiplexer_2_out), .sel(RY));  // open: en
  Register #(.width(16)) register_18 (.D(multiplexer_2_out), .en(undriven), .Q(RY_2), .clk(ClockBR));  // open: clr
endmodule

module ULA (
  input  in_1,
  input  Clock,
  input  [15:0] Dado1,
  input  [15:0] Dado_2,
  input  [2:0] ULAOP,
  output ZERO,
  output [15:0] ULA_RESULT
);

  wire comparator_1_lt;
  wire [15:0] adder_1_out, bit_extender_1_out, divider_1_out, multiplexer_1_out, multiplier_1_out,
       subtractor_1_out;

  Adder #(.width(16)) adder_1 (.a(Dado1), .b(Dado_2), .out(adder_1_out));  // open: cin, cout
  Subtractor #(.width(16)) subtractor_1 (.a(Dado1), .b(Dado_2), .out(subtractor_1_out));  // open: bin, bout
  Multiplier #(.width(16)) multiplier_1 (.a(Dado1), .b(Dado_2), .out(multiplier_1_out));  // open: cin, cout
  Divider #(.width(16)) divider_1 (.a(Dado1), .b(Dado_2), .out(divider_1_out));  // open: upper, rem
  Comparator #(.width(16)) comparator_1 (.a(Dado1), .b(Dado_2), .eq(ZERO), .lt(comparator_1_lt));  // open: gt
  Multiplexer #(.select(3), .width(16)) multiplexer_1 (
    .in0(adder_1_out), .in1(subtractor_1_out), .in2(multiplier_1_out), .in3(divider_1_out),
    .in4(bit_extender_1_out), .out(multiplexer_1_out), .sel(ULAOP));  // open: in5, in6, in7, en
  assign bit_extender_1_out = {{15{1'b0}}, comparator_1_lt};  // Bit_Extender bit_extender_1
  Register #(.width(16)) register_1 (.D(multiplexer_1_out), .Q(ULA_RESULT), .clk(Clock), .clr(in_1));  // open: en
endmodule

module Conversor_de_Saida (
  input  [15:0] in,
  output [3:0] out3,
  output [3:0] out2,
  output [3:0] out1,
  output [3:0] out0,
  output [11:0] out0_2
);


  assign out0 = in[3:0];
  assign out0_2 = in[11:0];
  assign out1 = in[7:4];
  assign out2 = in[11:8];
  assign out3 = in[15:12];
endmodule

module Clock (
  input  Reset,
  output _1,
  output _2,
  output _3,
  output _4,
  output _5
);

  wire and_1_out, Clock_out, not_1_out, not_2_out, not_3_out, not_4_out, not_5_out;

  Clock_part Clock (.out(Clock_out));
  D_Flip_Flop d_ff_1 (.clk(Clock_out), .D(and_1_out), .Q(_1), .reset(Reset));  // open: Qn, preset, en
  not not_1 (not_1_out, _1);
  D_Flip_Flop d_ff_2 (.clk(Clock_out), .D(_1), .Q(_2), .reset(Reset));  // open: Qn, preset, en
  D_Flip_Flop d_ff_3 (.clk(Clock_out), .D(_2), .Q(_3), .reset(Reset));  // open: Qn, preset, en
  not not_2 (not_2_out, _2);
  and and_1 (and_1_out, not_1_out, not_2_out, not_3_out, not_4_out, not_5_out);
  not not_3 (not_3_out, _3);
  D_Flip_Flop d_ff_4 (.clk(Clock_out), .D(_3), .Q(_4), .reset(Reset));  // open: Qn, preset, en
  not not_4 (not_4_out, _4);
  D_Flip_Flop d_ff_5 (.clk(Clock_out), .D(_4), .Q(_5), .reset(Reset));  // open: Qn, preset, en
  not not_5 (not_5_out, _5);
endmodule

module UNIDADE_DE_CONTROLE (
  input  in_1,
  input  in_2,
  input  in_3,
  input  in_4,
  output Jump,
  output ALUscr,
  output RW,
  output [2:0] ULAOP,
  output ALUadr,
  output ULA_MEM,
  output MemWrite,
  output Branch
);

  wire and_9_out, or_1_out, or_2_out, or_6_out, or_7_out, or_8_out, or_9_out;
  wire [1:0] not_10_out;
  wire [1:1] not_11_out;
  wire [2:0] not_1_out, not_7_out;
  wire [2:1] not_4_out;
  wire [2:2] not_8_out;
  wire [7:0] and_8_out;

  and and_1 (and_8_out[7], ~in_1, ~in_2, ~in_3, ~in_4);  // AND_Gate
  and and_2 (and_8_out[6], in_1, ~in_2, ~in_3, ~in_4);  // AND_Gate
  and and_3 (and_8_out[5], ~in_1, in_2, ~in_3, ~in_4);  // AND_Gate
  and and_4 (and_8_out[4], in_1, in_2, ~in_3, ~in_4);  // AND_Gate
  and and_5 (and_8_out[3], ~in_1, ~in_2, in_3, ~in_4);  // AND_Gate
  and and_6 (and_8_out[2], in_1, ~in_2, in_3, ~in_4);  // AND_Gate
  and and_7 (and_8_out[1], ~in_1, in_2, in_3, ~in_4);  // AND_Gate
  and and_8 (and_8_out[0], in_1, in_2, in_3, ~in_4);  // AND_Gate
  and and_9 (and_9_out, ~in_1, ~in_2, ~in_3, in_4);  // AND_Gate
  and and_10 (Branch, in_1, ~in_2, ~in_3, in_4);  // AND_Gate
  // AND_Gate and_11 has open pins: in0=in_4, in1=in_3, in2=in_2, in3=in_1, out=open
  // AND_Gate and_12 has open pins: in0=in_4, in1=in_3, in2=in_2, in3=in_1, out=open
  and and_13 (MemWrite, in_4, in_3, ~in_2, ~in_1);  // AND_Gate
  or or_1 (or_1_out, ULA_MEM, and_9_out);
  or or_2 (or_2_out, and_8_out[3], and_8_out[2], and_8_out[1], and_8_out[0], or_1_out);
  and and_14 (ULA_MEM, in_4, in_3, ~in_2, in_1);  // AND_Gate
  or or_3 (ALUscr, and_8_out[7], and_8_out[6], and_8_out[5], and_8_out[4]);
  or or_4 (RW, and_8_out[7], and_8_out[6], and_8_out[5], and_8_out[4], or_2_out);
  or or_5 (ALUadr, Branch, ULA_MEM, MemWrite);
  and and_15 (Jump, in_4, in_3, in_2, ~in_1);  // AND_Gate
  // AND_Gate and_16 has open pins: in0=in_4, in1=in_3, in2=in_2, in3=in_1, out=open
  not not_1 (not_1_out[0], 1'b1);
  not not_2 (not_1_out[1], 1'b1);
  not not_3 (not_1_out[2], 1'b1);
  assign ULAOP = or_6_out ? not_1_out : 3'bz;  // Controlled_Buffer controlled_buffer_1
  or or_6 (or_6_out, and_8_out[7], and_8_out[3], ULA_MEM, MemWrite);
  not not_4 (not_4_out[1], 1'b1);
  not not_5 (not_7_out[2], 1'b1);
  not not_6 (not_4_out[2], 1'b1);
  assign ULAOP = or_7_out ? {not_4_out, 1'b1} : 3'bz;  // Controlled_Buffer controlled_buffer_2
  or or_7 (or_7_out, and_8_out[6], and_8_out[2]);
  not not_7 (not_7_out[0], 1'b1);
  not not_8 (not_8_out[2], 1'b1);
  assign ULAOP = or_8_out ? {not_7_out[2], 1'b1, not_7_out[0]} : 3'bz;  // Controlled_Buffer controlled_buffer_3
  assign ULAOP = or_9_out ? {not_8_out[2], 2'b11} : 3'bz;  // Controlled_Buffer controlled_buffer_4
  or or_8 (or_8_out, and_8_out[5], and_8_out[1]);
  not not_9 (not_10_out[1], 1'b1);
  not not_10 (not_10_out[0], 1'b1);
  assign ULAOP = and_9_out ? {1'b1, not_10_out} : 3'bz;  // Controlled_Buffer controlled_buffer_5
  or or_9 (or_9_out, and_8_out[4], and_8_out[0]);
  not not_11 (not_11_out[1], 1'b1);
  assign ULAOP = Branch ? {1'b1, not_11_out[1], 1'b1} : 3'bz;  // Controlled_Buffer controlled_buffer_6
endmodule
