// Logisim project Registrador.circ as structural Verilog: 1 circuit, main circuit main
module main (
  input  in_1,
  input  in_2,
  output out_3,
  output out_4
);

  wire or_1_out, or_2_out;

  Register register_1 ();  // open: D, en, Q, clk, clr
  or or_1 (or_1_out, in_1, out_4);
  or or_2 (or_2_out, out_3, in_2);
  not not_1 (out_3, or_1_out);
  not not_2 (out_4, or_2_out);
endmodule
